# Fritzing sketch Sketch (saved by Fritzing 1.0.6)
breadboards: 1

parts:
  U1 = NodeMCU V1.0
  Part1 = SRF05 Ultrasonic Rangefinder
  U2 = WS2812 RGB LED strip

nets:
  N1: U1.D1, Part1.Trig
  N2: U1.D2, Part1.Echo
  VCC: U1.3V3, Part1.VCC, U2.VCC
  GND: U1.GND, Part1.GND, U2.GND
  N3: U1.D5, U2.DIN

custom parts:
  NodeMCU V1.0: ESP8266 based NodeMCU
  WS2812 RGB LED strip: WS2812 strip
